// Logisim project 10.circ as structural Verilog: 1 circuit, main circuit main
module main (
  input  X0,
  input  Y0,
  input  X1,
  input  Y1,
  output P0,
  output P1,
  output P2,
  output P3
);

  wire and_2_out, and_3_out, and_4_out, and_5_out, and_6_out;

  and and_1 (P0, X0, Y0);
  and and_2 (and_2_out, Y0, X0);
  and and_3 (and_3_out, X0, Y1);
  and and_4 (and_4_out, X0, Y1);
  and and_5 (and_5_out, X0, X0);
  and and_6 (and_6_out, Y1, Y0);
  and and_7 (P3, and_5_out, and_6_out);
  xor xor_1 (P1, and_2_out, and_3_out);
  xor xor_2 (P2, and_4_out, P3);

  assign X1 = X0;
endmodule
